// Digital circuit ex1.dig as structural Verilog
module ex1 (
  input  A,
  input  B,
  input  C,
  output X,
  output Y,
  output Z
);

  wire A2, and_1_out, and_2_out, and_3_out, and_4_out, and_5_out, and_6_out, and_7_out, and_8_out, and_9_out,
       and_10_out, B2, C2;

  not not_1 (A2, A);
  not not_2 (B2, B);
  and and_1 (and_1_out, A, B);
  and and_2 (and_2_out, A2, C2);
  and and_3 (and_3_out, C2, B);
  and and_4 (and_4_out, A, B2, C2);
  and and_5 (and_5_out, B2, C);
  and and_6 (and_6_out, C2, B);
  and and_7 (and_7_out, A2, B2, C2);
  and and_8 (and_8_out, A, B, C);
  and and_9 (and_9_out, A, B2, C);
  and and_10 (and_10_out, A2, B2, C2);
  not not_3 (C2, C);
  or or_1 (X, and_1_out, and_2_out, and_3_out);
  or or_2 (Y, and_4_out, and_5_out, and_6_out, and_7_out);
  or or_3 (Z, and_8_out, and_9_out, and_10_out);

  // Other names for the same wires on the sheet: A1 = A; B1 = B; C1 = C
endmodule

/* Test case EX1 Test:
A B C X Y Z

loop(A,2)
   loop(B,2)
      loop(C,2)
         bits(1,A) bits(1,B) bits(1,C) bits(1, (!A&!C) | (A&B)) bits(1, !B|!C) bits(1, (!A&!B&!C) | (A&C))
      end loop
   end loop
end loop
*/
